// Logisim project Atividade_Eletronica_Digital.circ as structural Verilog: 3 circuits, main circuit main
module main (
);

  wire clock_1_out, controle_1_j0, controle_1_j1, controle_1_j2, controle_1_j3, controle_1_k0, controle_1_k1,
       controle_1_k2, controle_1_k3, display_1_a, display_1_b, display_1_c, display_1_d, display_1_e,
       display_1_f, display_1_g, j_k_ff_1_q, j_k_ff_2_q, j_k_ff_3_q, j_k_ff_4_q;

  controle controle_1 (
    .Q3(j_k_ff_1_q), .Q2(j_k_ff_2_q), .Q1(j_k_ff_3_q), .Q0(j_k_ff_4_q), .J3(controle_1_j3),
    .K3(controle_1_k3), .J2(controle_1_j2), .K2(controle_1_k2), .J1(controle_1_j1), .K1(controle_1_k1),
    .J0(controle_1_j0), .K0(controle_1_k0));
  Clock clock_1 (.out(clock_1_out));
  J_K_Flip_Flop j_k_ff_1 (
    .J(controle_1_j3), .K(controle_1_k3), .clk(clock_1_out), .Q(j_k_ff_1_q));  // open: Qn, preset, reset
  J_K_Flip_Flop j_k_ff_2 (
    .J(controle_1_j2), .K(controle_1_k2), .clk(clock_1_out), .Q(j_k_ff_2_q));  // open: Qn, preset, reset
  display display_1 (
    .X3(j_k_ff_1_q), .X2(j_k_ff_2_q), .X1(j_k_ff_3_q), .X0(j_k_ff_4_q), .A(display_1_a), .B(display_1_b),
    .C(display_1_c), .D(display_1_d), .E(display_1_e), .F(display_1_f), .G(display_1_g));
  J_K_Flip_Flop j_k_ff_3 (
    .J(controle_1_j1), .K(controle_1_k1), .clk(clock_1_out), .Q(j_k_ff_3_q));  // open: Qn, preset, reset
  _7_Segment_Display u_7_segment_display_1 (
    .g(display_1_g), .f(display_1_f), .a(display_1_a), .b(display_1_b), .e(display_1_e), .d(display_1_d),
    .c(display_1_c));  // open: dp
  J_K_Flip_Flop j_k_ff_4 (
    .J(controle_1_j0), .K(controle_1_k0), .clk(clock_1_out), .Q(j_k_ff_4_q));  // open: Qn, preset, reset
endmodule

module controle (
  input  Q3,
  input  Q2,
  input  Q1,
  input  Q0,
  output J3,
  output K3,
  output J2,
  output K2,
  output J1,
  output K1,
  output J0,
  output K0
);

  wire and_1_out, and_2_out, and_3_out, and_4_out, and_5_out, and_6_out, and_7_out, and_8_out, not_1_out,
       not_2_out, not_3_out, not_4_out;

  not not_1 (not_1_out, Q3);
  not not_2 (not_2_out, Q2);
  not not_3 (not_3_out, Q1);
  not not_4 (not_4_out, Q0);
  and and_1 (and_1_out, not_2_out, not_3_out, not_4_out);
  and and_2 (and_2_out, Q2, Q1, not_4_out);
  and and_3 (and_3_out, not_3_out, Q0);
  and and_4 (and_4_out, Q1, not_4_out);
  and and_5 (and_5_out, Q2, not_4_out);
  and and_6 (and_6_out, Q3, not_4_out);
  and and_7 (and_7_out, not_2_out, Q0);
  and and_8 (and_8_out, Q2, not_4_out);
  and and_9 (J0, not_2_out, not_3_out);
  and and_10 (K0, not_1_out, not_2_out);
  or or_1 (J3, and_1_out, and_2_out);
  or or_2 (J2, and_3_out, and_4_out, Q3);
  or or_3 (J1, and_5_out, and_6_out);
  or or_4 (K1, and_7_out, and_8_out);

  assign K2 = 1'b1;
  assign K3 = 1'b1;
endmodule

module display (
  input  X3,
  input  X2,
  input  X1,
  input  X0,
  output A,
  output B,
  output C,
  output D,
  output E,
  output F,
  output G
);

  wire and_1_out, and_2_out, and_3_out, and_4_out, and_5_out, and_6_out, and_7_out, and_8_out, and_9_out,
       and_10_out, and_11_out, and_12_out, and_13_out, and_14_out, and_15_out, and_16_out, and_17_out,
       and_18_out, and_19_out, and_20_out, and_21_out, and_22_out, and_23_out, and_24_out, and_25_out,
       and_26_out, not_1_out, not_2_out, not_3_out, not_4_out;

  not not_1 (not_1_out, X3);
  not not_2 (not_2_out, X2);
  not not_3 (not_3_out, X1);
  not not_4 (not_4_out, X0);
  and and_1 (and_1_out, not_1_out, X1);
  and and_2 (and_2_out, not_1_out, X2, X0);
  and and_3 (and_3_out, X3, not_2_out, not_3_out);
  and and_4 (and_4_out, not_1_out, not_2_out, not_4_out);
  and and_5 (and_5_out, not_1_out, not_2_out);
  and and_6 (and_6_out, not_1_out, not_3_out, not_4_out);
  and and_7 (and_7_out, not_2_out, not_3_out);
  and and_8 (and_8_out, not_1_out, X1, X0);
  and and_9 (and_9_out, not_1_out, X0);
  and and_10 (and_10_out, not_2_out, not_3_out);
  and and_11 (and_11_out, not_1_out, X2);
  and and_12 (and_12_out, not_1_out, not_2_out, X1);
  and and_13 (and_13_out, not_1_out, X2, not_3_out, X0);
  and and_14 (and_14_out, X3, not_2_out, not_3_out);
  and and_15 (and_15_out, not_1_out, not_2_out, not_4_out);
  and and_16 (and_16_out, not_1_out, X1, not_4_out);
  and and_17 (and_17_out, not_1_out, X1, not_4_out);
  and and_18 (and_18_out, not_2_out, not_3_out, not_4_out);
  and and_19 (and_19_out, not_1_out, X2, not_3_out);
  and and_20 (and_20_out, not_1_out, X2, not_4_out);
  and and_21 (and_21_out, X3, not_2_out, not_3_out);
  and and_22 (and_22_out, not_1_out, not_3_out, not_4_out);
  and and_23 (and_23_out, not_1_out, not_2_out, X1);
  and and_24 (and_24_out, X3, not_2_out, not_3_out);
  and and_25 (and_25_out, not_1_out, X2, not_3_out);
  and and_26 (and_26_out, not_1_out, X2, not_4_out);
  or or_1 (A, and_1_out, and_2_out, and_3_out, and_4_out);
  or or_2 (B, and_5_out, and_6_out, and_7_out, and_8_out);
  or or_3 (C, and_9_out, and_10_out, and_11_out);
  or or_4 (D, and_12_out, and_13_out, and_14_out, and_15_out, and_16_out);
  or or_5 (E, and_17_out, and_18_out);
  or or_6 (F, and_19_out, and_20_out, and_21_out, and_22_out);
  or or_7 (G, and_23_out, and_24_out, and_25_out, and_26_out);
endmodule
